// Logisim project sap1.circ as structural Verilog
module ProgramCounter (
  input  Cp,
  input  Clk,
  input  Clr,
  input  En,
  output [3:0] out_5
);

  wire halfaddress_1_carry, halfaddress_2_carry, halfaddress_2_soma, halfaddress_3_carry, halfaddress_3_soma,
       halfaddress_4_carry, halfaddress_4_soma, not_1_out;
  wire [3:0] d_ff_4_q;

  not not_1 (not_1_out, Clk);
  HalfAddress halfaddress_1 (.Carry(halfaddress_1_carry), .A(halfaddress_2_carry), .B(d_ff_4_q[3]));  // open: Soma
  D_Flip_Flop d_ff_1 (.clk(not_1_out), .D(halfaddress_1_carry), .Q(d_ff_4_q[3]), .reset(Clr));  // open: Qn, preset, en
  HalfAddress halfaddress_2 (
    .Soma(halfaddress_2_soma), .Carry(halfaddress_2_carry), .A(halfaddress_3_carry), .B(d_ff_4_q[2]));
  D_Flip_Flop d_ff_2 (.clk(not_1_out), .D(halfaddress_2_soma), .Q(d_ff_4_q[2]), .reset(Clr));  // open: Qn, preset, en
  HalfAddress halfaddress_3 (
    .Soma(halfaddress_3_soma), .Carry(halfaddress_3_carry), .A(halfaddress_4_carry), .B(d_ff_4_q[1]));
  D_Flip_Flop d_ff_3 (.clk(not_1_out), .D(halfaddress_3_soma), .Q(d_ff_4_q[1]), .reset(Clr));  // open: Qn, preset, en
  HalfAddress halfaddress_4 (.Soma(halfaddress_4_soma), .Carry(halfaddress_4_carry), .A(Cp), .B(d_ff_4_q[0]));
  D_Flip_Flop d_ff_4 (.clk(not_1_out), .D(halfaddress_4_soma), .Q(d_ff_4_q[0]), .reset(Clr));  // open: Qn, preset, en
  assign out_5 = En ? d_ff_4_q : 4'bz;  // Controlled_Buffer controlled_buffer_1
endmodule

module HalfAddress (
  input  A,
  input  B,
  output Soma,
  output Carry
);

  xor xor_1 (Soma, B, A);
  and and_1 (Carry, A, B);
endmodule

module MAR (
  input  Clk,
  input  Clr,
  input  [3:0] In,
  input  in_4,
  output [3:0] out_5
);

  wire not_1_out;
  wire [3:0] controlled_buffer_1_out;

  assign controlled_buffer_1_out = not_1_out ? In : 4'bz;  // Controlled_Buffer controlled_buffer_1
  not not_1 (not_1_out, in_4);
  D_Flip_Flop d_ff_1 (.clk(Clk), .D(controlled_buffer_1_out[3]), .Q(out_5[3]), .reset(Clr));  // open: Qn, preset, en
  D_Flip_Flop d_ff_2 (.clk(Clk), .D(controlled_buffer_1_out[2]), .Q(out_5[2]), .reset(Clr));  // open: Qn, preset, en
  D_Flip_Flop d_ff_3 (.clk(Clk), .D(controlled_buffer_1_out[1]), .Q(out_5[1]), .reset(Clr));  // open: Qn, preset, en
  D_Flip_Flop d_ff_4 (.clk(Clk), .D(controlled_buffer_1_out[0]), .Q(out_5[0]), .reset(Clr));  // open: Qn, preset, en
endmodule
